// Logisim project Taller1.circ as structural Verilog: 9 circuits, main circuit sumador_simple
module sumador_simple (
  input  A,
  input  B,
  output S,
  output Cout
);

  xor xor_1 (S, A, B);
  and and_1 (Cout, A, B);
endmodule

module sumador_completo (
  input  Cin,
  input  A,
  input  B,
  output S,
  output Cout
);

  wire sumador_simple_1_cout, sumador_simple_1_s, sumador_simple_2_cout;

  sumador_simple sumador_simple_1 (.A(A), .B(B), .S(sumador_simple_1_s), .Cout(sumador_simple_1_cout));
  sumador_simple sumador_simple_2 (.A(Cin), .B(sumador_simple_1_s), .S(S), .Cout(sumador_simple_2_cout));
  or or_1 (Cout, sumador_simple_2_cout, sumador_simple_1_cout);
endmodule

module sumador_4 (
  input  Cin,
  input  [3:0] A,
  input  [3:0] B,
  output [3:0] S,
  output Cout
);

  wire sumador_completo_1_cout, sumador_completo_2_cout, sumador_completo_3_cout;

  sumador_completo sumador_completo_1 (.Cin(Cin), .A(A[0]), .B(B[0]), .S(S[0]), .Cout(sumador_completo_1_cout));
  sumador_completo sumador_completo_2 (
    .Cin(sumador_completo_1_cout), .A(A[1]), .B(B[1]), .S(S[1]), .Cout(sumador_completo_2_cout));
  sumador_completo sumador_completo_3 (
    .Cin(sumador_completo_2_cout), .A(A[2]), .B(B[2]), .S(S[2]), .Cout(sumador_completo_3_cout));
  sumador_completo sumador_completo_4 (.Cin(sumador_completo_3_cout), .A(A[3]), .B(B[3]), .S(S[3]), .Cout(Cout));
  Hex_Digit_Display hex_digit_display_1 (.value(S));  // open: dp
endmodule

module comparador_cero (
  input  [3:0] A,
  input  [3:0] in_2,
  input  [3:0] in_3,
  output Z,
  output out_5,
  output out_6
);

  wire and_2_out, and_3_out, and_4_out, and_5_out, and_6_out, and_7_out, and_8_out, and_9_out, and_10_out,
       and_11_out, not_1_out, not_2_out, not_3_out, not_4_out, not_6_out, not_7_out, not_8_out, not_9_out,
       or_1_out, or_2_out, or_3_out;

  not not_1 (not_1_out, A[0]);
  not not_2 (not_2_out, A[1]);
  not not_3 (not_3_out, A[2]);
  not not_4 (not_4_out, A[3]);
  or or_1 (or_1_out, in_3[0], in_3[1]);
  or or_2 (or_2_out, in_3[2], in_3[3]);
  or or_3 (or_3_out, or_1_out, or_2_out);
  and and_1 (Z, not_1_out, not_2_out, not_3_out, not_4_out);
  not not_5 (out_6, or_3_out);
  not not_6 (not_6_out, in_2[0]);
  not not_7 (not_7_out, in_2[1]);
  not not_8 (not_8_out, in_2[2]);
  not not_9 (not_9_out, in_2[3]);
  and and_2 (and_2_out, not_6_out, not_7_out);
  and and_3 (and_3_out, not_6_out, not_8_out);
  and and_4 (and_4_out, not_6_out, not_9_out);
  and and_5 (and_5_out, not_7_out, not_8_out);
  and and_6 (and_6_out, not_7_out, not_9_out);
  and and_7 (and_7_out, not_8_out, not_9_out);
  and and_8 (and_8_out, and_2_out, and_3_out);
  and and_9 (and_9_out, and_4_out, and_5_out);
  and and_10 (and_10_out, and_6_out, and_7_out);
  and and_11 (and_11_out, and_8_out, and_9_out);
  and and_12 (out_5, and_11_out, and_10_out);
endmodule

module sumador_flags (
  input  Cin,
  input  [3:0] A,
  input  [3:0] B,
  output [3:0] S,
  output Z,
  output C,
  output N,
  output V
);

  wire xnor_1_out;

  xnor xnor_1 (xnor_1_out, A[3], B[3]);
  sumador_4 sumador_4_1 (.Cin(Cin), .A(A), .B(B), .S({N, S[2:0]}), .Cout(C));
  comparador_cero comparador_cero_1 (.A({N, S[2:0]}), .Z(Z));  // open: in_2, in_3, out_5, out_6
  xnor xnor_2 (V, xnor_1_out, N);
  Hex_Digit_Display hex_digit_display_1 (.value({N, S[2:0]}));  // open: dp

  assign S[3] = N;
endmodule

module incrementador_4 (
  input  [3:0] A,
  output [3:0] S
);

  sumador_4 sumador_4_1 (.Cin(1'b1), .A(A), .S(S));  // open: B, Cout
  Hex_Digit_Display hex_digit_display_1 (.value(S));  // open: dp
endmodule

module inversor_4 (
  input  [3:0] in_1,
  input  in_2,
  output [3:0] out_3
);

  wire [3:0] incrementador_4_1_s, xor_1_out;

  xor xor_1 (xor_1_out[0], in_1[0], in_2);
  xor xor_2 (xor_1_out[1], in_1[1], in_2);
  xor xor_3 (xor_1_out[2], in_1[2], in_2);
  xor xor_4 (xor_1_out[3], in_1[3], in_2);
  Multiplexer #(.width(4)) multiplexer_1 (.in0(in_1), .in1(incrementador_4_1_s), .out(out_3), .sel(in_2));
  incrementador_4 incrementador_4_1 (.A(xor_1_out), .S(incrementador_4_1_s));
  Hex_Digit_Display hex_digit_display_1 (.value(out_3));  // open: dp
endmodule

module ALU (
  input  [3:0] A,
  input  [3:0] B,
  input  [1:0] OP,
  output [3:0] S,
  output Z,
  output C,
  output N,
  output V
);

  wire and_5_out, and_6_out, and_7_out, and_8_out, and_9_out, and_10_out, and_11_out, and_12_out,
       comparador_cero_1_z, comparador_cero_2_z, not_1_out, not_2_out, not_3_out, not_4_out, not_5_out,
       not_6_out, not_7_out, not_8_out, or_5_out, or_6_out, or_7_out, sumador_flags_1_c, sumador_flags_1_n,
       sumador_flags_1_v, sumador_flags_1_z, sumador_flags_2_n, sumador_flags_2_z;
  wire [3:0] and_1_out, inversor_4_1_out_3, or_1_out, sumador_flags_1_s, sumador_flags_2_s;

  inversor_4 inversor_4_1 (.in_1(B), .in_2(1'b1), .out_3(inversor_4_1_out_3));
  and and_1 (and_1_out[0], A[0], B[0]);
  and and_2 (and_1_out[1], A[1], B[1]);
  and and_3 (and_1_out[2], A[2], B[2]);
  and and_4 (and_1_out[3], A[3], B[3]);
  or or_1 (or_1_out[0], A[0], B[0]);
  or or_2 (or_1_out[1], A[1], B[1]);
  or or_3 (or_1_out[2], A[2], B[2]);
  or or_4 (or_1_out[3], A[3], B[3]);
  not not_1 (not_1_out, A[0]);
  not not_2 (not_2_out, A[1]);
  not not_3 (not_3_out, A[2]);
  not not_4 (not_4_out, A[3]);
  and and_5 (and_5_out, not_1_out, inversor_4_1_out_3[0]);
  and and_6 (and_6_out, not_2_out, inversor_4_1_out_3[1]);
  and and_7 (and_7_out, not_3_out, inversor_4_1_out_3[2]);
  and and_8 (and_8_out, not_4_out, inversor_4_1_out_3[3]);
  sumador_flags sumador_flags_1 (
    .A(A), .B(B), .S(sumador_flags_1_s), .Z(sumador_flags_1_z), .C(sumador_flags_1_c), .N(sumador_flags_1_n),
    .V(sumador_flags_1_v));  // open: Cin
  sumador_flags sumador_flags_2 (
    .A(A), .B(inversor_4_1_out_3), .S(sumador_flags_2_s), .Z(sumador_flags_2_z), .N(sumador_flags_2_n));  // open: Cin, C, V
  or or_5 (or_5_out, and_5_out, and_6_out);
  or or_6 (or_6_out, and_7_out, and_8_out);
  or or_7 (or_7_out, or_5_out, or_6_out);
  not not_5 (not_5_out, B[0]);
  not not_6 (not_6_out, B[1]);
  not not_7 (not_7_out, B[2]);
  buf and_9 (and_9_out, not_5_out);  // AND_Gate
  and and_10 (and_10_out, not_7_out, B[3]);
  Multiplexer #(.select(2), .width(4)) multiplexer_1 (
    .in0(sumador_flags_1_s), .in1(sumador_flags_2_s), .in2(and_1_out), .in3(or_1_out), .out(S), .sel(OP));
  and and_11 (and_11_out, and_9_out, and_10_out);
  comparador_cero comparador_cero_1 (.A(and_1_out), .Z(comparador_cero_1_z));  // open: in_2, in_3, out_5, out_6
  comparador_cero comparador_cero_2 (.A(or_1_out), .Z(comparador_cero_2_z));  // open: in_2, in_3, out_5, out_6
  not not_8 (not_8_out, A[0]);
  and and_12 (and_12_out, not_8_out, and_11_out);
  Hex_Digit_Display hex_digit_display_1 (.value(S));  // open: dp
  Multiplexer #(.select(2)) multiplexer_2 (
    .in0(sumador_flags_1_z), .in1(sumador_flags_2_z), .in2(comparador_cero_1_z), .in3(comparador_cero_2_z),
    .out(Z), .sel(OP));
  Multiplexer #(.select(2)) multiplexer_3 (
    .in0(sumador_flags_1_c), .in1(or_7_out), .out(C), .sel(OP));  // open: in2, in3
  Multiplexer #(.select(2)) multiplexer_4 (
    .in0(sumador_flags_1_n), .in1(sumador_flags_2_n), .in2(and_1_out[3]), .in3(or_1_out[3]), .out(N), .sel(OP));
  Multiplexer #(.select(2)) multiplexer_5 (
    .in0(sumador_flags_1_v), .in1(and_12_out), .out(V), .sel(OP));  // open: in2, in3
endmodule

module verificador (
  output [3:0] out_1,
  output [3:0] out_2,
  output [1:0] out_3,
  output halt,
  output N,
  output Z,
  output V,
  output C,
  output [3:0] res
);

  wire clock_1_out;

  Clock clock_1 (.out(clock_1_out));
  Counter #(.max('h3ff), .width(10)) counter_1 (
    .clk(clock_1_out), .carry(halt), .Q({out_3, out_2, out_1}));  // open: clr, load, up, count, D
  // ALU alu_1: pin names not known; wires that end beside it: out_1, out_2, out_3, N, Z, V, C, res
endmodule
