// Logisim project MaquinasDeEstadoFinitas.circ as structural Verilog
module Ejercicio1 (
  input  in_1
);

  wire and_1_out, clock_1_out, d_ff_1_q, d_ff_2_q, d_ff_2_qn;

  Clock clock_1 (.out(clock_1_out));
  LED led_1 (.in(d_ff_1_q));
  D_Flip_Flop d_ff_1 (.D(d_ff_2_qn), .clk(clock_1_out), .Q(d_ff_1_q), .reset(in_1));  // open: Qn, preset
  and and_1 (and_1_out, d_ff_2_qn, d_ff_1_q);
  D_Flip_Flop d_ff_2 (.D(and_1_out), .clk(clock_1_out), .Q(d_ff_2_q), .Qn(d_ff_2_qn), .preset(in_1));  // open: reset
  LED led_2 (.in(d_ff_2_q));
endmodule

module Ejercicio2 (
  input  in_1,
  input  in_2,
  output out_3,
  output out_4
);

  J_K_Flip_Flop j_k_ff_1 (.J(in_1), .K(in_1), .clk(in_2), .Q(out_4));  // open: Qn, preset, reset
  J_K_Flip_Flop j_k_ff_2 (.J(out_4), .K(out_4), .clk(in_2), .Q(out_3));  // open: Qn, preset, reset
endmodule

module Ejercicio3 (
  output out_1,
  output out_2
);

  wire clock_1_out, ejercicio2_1_out_3, ejercicio2_1_out_4;

  Clock clock_1 (.out(clock_1_out));
  Ejercicio2 ejercicio2_1 (.in_1(1'b1), .in_2(clock_1_out), .out_3(ejercicio2_1_out_3), .out_4(ejercicio2_1_out_4));
  or or_1 (out_1, ejercicio2_1_out_3, ejercicio2_1_out_4);
  and and_1 (out_2, ~ejercicio2_1_out_4, ejercicio2_1_out_3);  // AND_Gate
endmodule

module Ejercicio4 (
  input  in_1,
  output out_2,
  output out_3
);

  wire and_1_out, clock_1_out, ejercicio2_1_out_3, ejercicio2_1_out_4, or_1_out;

  Clock clock_1 (.out(clock_1_out));
  Ejercicio2 ejercicio2_1 (.in_1(1'b1), .in_2(clock_1_out), .out_3(ejercicio2_1_out_3), .out_4(ejercicio2_1_out_4));
  and and_1 (and_1_out, ejercicio2_1_out_3, ~ejercicio2_1_out_4);  // AND_Gate
  or or_1 (or_1_out, ejercicio2_1_out_3, ejercicio2_1_out_4);
  xor xor_1 (out_2, in_1, and_1_out);
  xor xor_2 (out_3, in_1, or_1_out);
endmodule

module EjercicioB1 (
  input  in_1,
  output out_2,
  output out_3
);

  wire clock_1_out, d_ff_1_qn, xnor_1_out;

  Clock clock_1 (.out(clock_1_out));
  D_Flip_Flop d_ff_1 (.D(d_ff_1_qn), .clk(clock_1_out), .Q(out_2), .Qn(d_ff_1_qn), .reset(in_1));  // open: preset
  xnor xnor_1 (xnor_1_out, out_3, out_2);
  D_Flip_Flop d_ff_2 (.D(xnor_1_out), .clk(clock_1_out), .Q(out_3), .reset(in_1));  // open: Qn, preset
endmodule
